# Fritzing sketch controller (saved by Fritzing 0.7.7b)

parts:
  Rpd = Resistor [tolerance=±5% resistance=1k package=THT]
  MTR_SW = female pin header, 2 pins [form="♀ (female)"]
  SMDv2_3 = female pin header, 4 pins [form="♀ (female)"]
  -5V+ = female pin header, 2 pins [form="♀ (female)"]
  POTI = Rotary Potentiometer (Small) [maximum_resistance=100kΩ]
  Arduino_Pro_Mega = Arduino Pro Mini 3.3V

nets:
  N1: Rpd.Pin_0, Arduino_Pro_Mega.D2
  N2: Rpd.Pin_1, MTR_SW.pin1
  N3: MTR_SW.pin2, SMDv2_3.pin1, -5V+.pin2, POTI.leg1, Arduino_Pro_Mega.GND
  N4: SMDv2_3.pin2, Arduino_Pro_Mega.D4
  N5: SMDv2_3.pin3, Arduino_Pro_Mega.D5
  N6: SMDv2_3.pin4, Arduino_Pro_Mega.D6
  N7: -5V+.pin1, POTI.leg2, Arduino_Pro_Mega.VCC
  N8: POTI.wiper, Arduino_Pro_Mega.A2

notes:
  extruder controller v0.1.0
